// Logisim project Final logic edition-1.circ as structural Verilog: 1 circuit, main circuit main
module main (
  input  [2:0] A,
  input  [2:0] B,
  input  [1:0] Sub_00__Add_01_____Mul_10____Rim_11
);

  wire main_1_bit1, main_1_bit2, main_1_bit3, main_1_sign, main_2_bit1, main_2_bit2, main_2_bit3,
       main_2_bit4, main_2_minus_ve, main_3_p5, main_3_p7, n7_segment_display_driver_1_p5,
       n7_segment_display_driver_1_p6, n7_segment_display_driver_1_p7, n7_segment_display_driver_1_p8,
       n7_segment_display_driver_1_p9, n7_segment_display_driver_1_p10, n7_segment_display_driver_1_p11;
  wire [1:0] bit_extender_1_out, bit_extender_7_out, bit_extender_12_out;
  wire [2:0] bit_extender_3_out, bit_extender_6_out, bit_extender_14_out;
  wire [3:0] bit_extender_2_out, bit_extender_5_out, bit_extender_11_out, bit_extender_13_out;
  wire [4:0] bit_extender_4_out, bit_extender_8_out, bit_extender_10_out, bit_extender_15_out,
       multiplexer_1_out;
  wire [5:0] bit_extender_9_out, demultiplexer_1_out0, demultiplexer_1_out1, demultiplexer_1_out2,
       demultiplexer_1_out3, or_1_out;

  Demultiplexer #(.select(2), .width(6)) demultiplexer_1 (
    .out0(demultiplexer_1_out0), .out1(demultiplexer_1_out1), .out2(demultiplexer_1_out2),
    .out3(demultiplexer_1_out3), .in(bit_extender_9_out), .sel(Sub_00__Add_01_____Mul_10____Rim_11));  // open: en
  assign or_1_out = demultiplexer_1_out0 | demultiplexer_1_out1;  // OR_Gate or_1, 6 bits wide
  SUB_ADD_main main_1 (
    .ADD(Sub_00__Add_01_____Mul_10____Rim_11[0]), .S1(or_1_out[2]), .A1(or_1_out[1]), .A0(or_1_out[0]),
    .S2(or_1_out[5]), .B1(or_1_out[4]), .B0(or_1_out[3]), .Bit3(main_1_bit3), .Bit2(main_1_bit2),
    .Bit1(main_1_bit1), .Sign(main_1_sign));
  assign bit_extender_1_out = {{1{main_1_bit2}}, main_1_bit1};  // Bit_Extender bit_extender_1
  assign bit_extender_2_out = {{1{1'b0}}, bit_extender_3_out};  // Bit_Extender bit_extender_2
  assign bit_extender_3_out = {{1{main_1_bit3}}, bit_extender_1_out};  // Bit_Extender bit_extender_3
  assign bit_extender_4_out = {{1{main_1_sign}}, bit_extender_2_out};  // Bit_Extender bit_extender_4
  Multiplexer #(.select(2), .width(5)) multiplexer_1 (
    .in0(bit_extender_4_out), .in1(bit_extender_4_out), .in2(bit_extender_10_out), .in3(bit_extender_15_out),
    .out(multiplexer_1_out), .sel(Sub_00__Add_01_____Mul_10____Rim_11));  // open: en
  Multiplication_main main_2 (
    .B1(demultiplexer_1_out2[4]), .B0(demultiplexer_1_out2[3]), .A1(demultiplexer_1_out2[1]),
    .A0(demultiplexer_1_out2[0]), .S1(demultiplexer_1_out2[2]), .S2(demultiplexer_1_out2[5]),
    .Bit4(main_2_bit4), .Bit3(main_2_bit3), .Bit2(main_2_bit2), .Bit1(main_2_bit1), .minus_ve(main_2_minus_ve));
  assign bit_extender_5_out = {{1{B[0]}}, A};  // Bit_Extender bit_extender_5
  assign bit_extender_6_out = {{1{main_2_bit3}}, bit_extender_7_out};  // Bit_Extender bit_extender_6
  assign bit_extender_7_out = {{1{main_2_bit2}}, main_2_bit1};  // Bit_Extender bit_extender_7
  // _7_segment_display_driver 7_segment_display_driver_1: pin names not known; wires that end beside it: multiplexer_1_out[3], multiplexer_1_out[2], multiplexer_1_out[1], multiplexer_1_out[0], n7_segment_display_driver_1_p5, n7_segment_display_driver_1_p6, n7_segment_display_driver_1_p7, n7_segment_display_driver_1_p8, n7_segment_display_driver_1_p9, n7_segment_display_driver_1_p10, n7_segment_display_driver_1_p11
  assign bit_extender_8_out = {{1{B[1]}}, bit_extender_5_out};  // Bit_Extender bit_extender_8
  assign bit_extender_9_out = {{1{B[2]}}, bit_extender_8_out};  // Bit_Extender bit_extender_9
  assign bit_extender_10_out = {{1{main_2_minus_ve}}, bit_extender_11_out};  // Bit_Extender bit_extender_10
  assign bit_extender_11_out = {{1{main_2_bit4}}, bit_extender_6_out};  // Bit_Extender bit_extender_11
  _7_Segment_Display u_7_segment_display_1 (.g(multiplexer_1_out[4]));  // open: f, a, b, e, d, c, dp
  _7_Segment_Display u_7_segment_display_2 (
    .g(n7_segment_display_driver_1_p11), .f(n7_segment_display_driver_1_p10),
    .a(n7_segment_display_driver_1_p5), .b(n7_segment_display_driver_1_p6),
    .e(n7_segment_display_driver_1_p9), .d(n7_segment_display_driver_1_p8), .c(n7_segment_display_driver_1_p7));  // open: dp
  // Project_Reminder_main main_3: pin names not known; wires that end beside it: demultiplexer_1_out3[1], demultiplexer_1_out3[0], demultiplexer_1_out3[5], demultiplexer_1_out3[4], main_3_p5, demultiplexer_1_out3[3], main_3_p7
  assign bit_extender_12_out = {{1{main_3_p7}}, main_3_p5};  // Bit_Extender bit_extender_12
  assign bit_extender_13_out = {{1{1'b0}}, bit_extender_14_out};  // Bit_Extender bit_extender_13
  assign bit_extender_14_out = {{1{1'b0}}, bit_extender_12_out};  // Bit_Extender bit_extender_14
  assign bit_extender_15_out = {{1{1'b0}}, bit_extender_13_out};  // Bit_Extender bit_extender_15

  // Notes on the sheet:
  //   B then A
endmodule
