// Logisim project Multiplication.circ as structural Verilog: 1 circuit, main circuit main
module main (
  input  B1,
  input  B0,
  input  A1,
  input  A0,
  input  S1,
  input  S2,
  output minus_ve,
  output Bit4,
  output Bit3,
  output Bit2,
  output Bit1
);

  wire adder_1_cout, and_1_out, and_2_out, and_3_out, n7_segment_display_driver_1_p5,
       n7_segment_display_driver_1_p6, n7_segment_display_driver_1_p7, n7_segment_display_driver_1_p8,
       n7_segment_display_driver_1_p9, n7_segment_display_driver_1_p10, n7_segment_display_driver_1_p11;

  and and_1 (and_1_out, B1, A1);
  and and_2 (and_2_out, B1, A0);
  and and_3 (and_3_out, B0, A1);
  and and_4 (Bit1, B0, A0);
  Adder #(.width(1)) adder_1 (.a(and_2_out), .b(and_3_out), .out(Bit2), .cin(1'b0), .cout(adder_1_cout));
  Adder #(.width(1)) adder_2 (.a(1'b0), .b(and_1_out), .out(Bit3), .cin(adder_1_cout), .cout(Bit4));
  xor xor_1 (minus_ve, S2, S1);
  LED led_1 (.in(minus_ve));
  // _7_segment_display_driver 7_segment_display_driver_1: pin names not known; wires that end beside it: Bit4, Bit3, Bit2, Bit1, n7_segment_display_driver_1_p5, n7_segment_display_driver_1_p6, n7_segment_display_driver_1_p7, n7_segment_display_driver_1_p8, n7_segment_display_driver_1_p9, n7_segment_display_driver_1_p10, n7_segment_display_driver_1_p11
  _7_Segment_Display u_7_segment_display_1 (.g(minus_ve));  // open: f, a, b, e, d, c, dp
  _7_Segment_Display u_7_segment_display_2 (
    .g(n7_segment_display_driver_1_p11), .f(n7_segment_display_driver_1_p10),
    .a(n7_segment_display_driver_1_p5), .b(n7_segment_display_driver_1_p6),
    .e(n7_segment_display_driver_1_p9), .d(n7_segment_display_driver_1_p8), .c(n7_segment_display_driver_1_p7));  // open: dp
endmodule
