// Logisim project Project_Reminder.circ as structural Verilog: 1 circuit, main circuit main
module main (
  input  minus_ve_A,
  input  A_2,
  input  A_1,
  input  minus_ve_B,
  input  B_2,
  input  B_1,
  input  in_7
);

  wire and_3_out, and_4_out, multiplexer_1_out, n7_segment_display_driver_1_p5,
       n7_segment_display_driver_1_p6, n7_segment_display_driver_1_p7, n7_segment_display_driver_1_p8,
       n7_segment_display_driver_1_p9, n7_segment_display_driver_1_p10, n7_segment_display_driver_1_p11,
       nor_1_out, nor_2_out, not_1_out, not_2_out, not_3_out, or_1_out, or_2_out, or_3_out;
  wire [1:0] and_1_out, n7_segment_display_driver_1_p3;

  not not_1 (not_1_out, B_1);
  not not_2 (not_2_out, A_2);
  nor nor_1 (nor_1_out, B_1, B_2);
  not not_3 (not_3_out, A_1);
  LED div__by_Zero_Flag (.in(nor_1_out));
  or or_1 (or_1_out, not_1_out, not_2_out);
  and and_1 (and_1_out[0], not_3_out, A_2, B_2, B_1);
  and and_2 (and_1_out[1], B_2, A_1, or_1_out);
  LED _2 (.in(and_1_out[0]));
  LED _1 (.in(and_1_out[1]));
  or or_2 (or_2_out, and_1_out[1], and_1_out[0]);
  nor nor_2 (nor_2_out, and_1_out[0], and_1_out[1]);
  or or_3 (or_3_out, B_1, B_2);
  Multiplexer multiplexer_1 (.in0(in_7), .out(multiplexer_1_out), .sel(nor_1_out));  // open: in1, en
  // _7_segment_display_driver 7_segment_display_driver_1: pin names not known; wires that end beside it: multiplexer_1_out, multiplexer_1_out, n7_segment_display_driver_1_p3[0], n7_segment_display_driver_1_p3[1], n7_segment_display_driver_1_p5, n7_segment_display_driver_1_p6, n7_segment_display_driver_1_p7, n7_segment_display_driver_1_p8, n7_segment_display_driver_1_p9, n7_segment_display_driver_1_p10, n7_segment_display_driver_1_p11
  Multiplexer #(.width(2)) multiplexer_2 (
    .in0(and_1_out), .out(n7_segment_display_driver_1_p3), .sel(nor_1_out));  // open: in1, en
  and and_3 (and_3_out, nor_2_out, or_3_out);
  LED minus_ve_Flag (.in(and_4_out));
  and and_4 (and_4_out, minus_ve_A, or_2_out);
  LED Zero_flag (.in(and_3_out));
  _7_Segment_Display u_7_segment_display_1 (
    .g(n7_segment_display_driver_1_p11), .f(n7_segment_display_driver_1_p10),
    .a(n7_segment_display_driver_1_p5), .b(n7_segment_display_driver_1_p6),
    .e(n7_segment_display_driver_1_p9), .d(n7_segment_display_driver_1_p8), .c(n7_segment_display_driver_1_p7));  // open: dp
  _7_Segment_Display u_7_segment_display_2 (.g(and_4_out));  // open: f, a, b, e, d, c, dp
endmodule
