// Logisim project SUB&ADD.circ as structural Verilog: 1 circuit, main circuit main
module main (
  input  ADD,
  input  S1,
  input  A1,
  input  A0,
  input  S2,
  input  B1,
  input  B0,
  output Sign,
  output Bit3,
  output Bit2,
  output Bit1
);

  wire adder_1_cout, adder_1_out, adder_2_cout, adder_2_out, and_1_out, and_2_out, and_3_out, and_4_out,
       and_5_out, and_6_out, and_7_out, ic_7485_1_p12, ic_7485_1_p13, multiplexer_1_out, multiplexer_5_out,
       n7_segment_display_driver_1_p5, n7_segment_display_driver_1_p6, n7_segment_display_driver_1_p7,
       n7_segment_display_driver_1_p8, n7_segment_display_driver_1_p9, n7_segment_display_driver_1_p10,
       n7_segment_display_driver_1_p11, nor_1_out, not_1_out, not_2_out, not_3_out, not_4_out, not_5_out,
       not_6_out, not_7_out, or_1_out, or_2_out, or_3_out, or_4_out, or_5_out, xnor_1_out, xor_1_out,
       xor_2_out;

  not not_1 (not_1_out, B0);
  not not_2 (not_2_out, A0);
  not not_3 (not_3_out, B1);
  not not_4 (not_4_out, A1);
  and and_1 (and_1_out, A1, not_3_out);
  and and_2 (and_2_out, and_1_out, or_1_out);
  or or_1 (or_1_out, A0, not_1_out);
  and and_3 (and_3_out, not_4_out, B1);
  and and_4 (and_4_out, and_3_out, or_2_out);
  or or_2 (or_2_out, B0, not_2_out);
  not not_5 (not_5_out, ADD);
  xor xor_1 (xor_1_out, S2, S1);
  and and_5 (and_5_out, not_5_out, xor_1_out);
  or or_3 (or_3_out, and_2_out, and_4_out);
  xor xor_2 (xor_2_out, A0, B0);
  // IC_7485 ic_7485_1: pin names not known; wires that end beside it: A0, A1, 1'b0, 1'b0, B0, B1, 1'b0, 1'b0, 1'b0, 1'b0, 1'b0, ic_7485_1_p12, ic_7485_1_p13
  xnor xnor_1 (xnor_1_out, S2, S1);
  and and_6 (and_6_out, xnor_1_out, ADD);
  or or_4 (or_4_out, and_5_out, and_6_out);
  nor nor_1 (nor_1_out, ic_7485_1_p12, ic_7485_1_p13);
  and and_7 (and_7_out, nor_1_out, not_7_out);
  not not_6 (not_6_out, S1);
  Multiplexer multiplexer_1 (.in0(S1), .in1(not_6_out), .out(multiplexer_1_out), .sel(and_7_out));  // open: en
  Adder #(.width(1)) adder_1 (.a(A1), .b(B1), .out(adder_1_out), .cin(adder_2_cout), .cout(adder_1_cout));
  Adder #(.width(1)) adder_2 (.a(A0), .b(B0), .out(adder_2_out), .cin(1'b0), .cout(adder_2_cout));
  Multiplexer multiplexer_2 (.in0(or_3_out), .in1(adder_1_out), .out(Bit2), .sel(or_4_out));  // open: en
  Multiplexer multiplexer_3 (.in0(1'b0), .in1(adder_1_cout), .out(Bit3), .sel(or_4_out));  // open: en
  Multiplexer multiplexer_4 (.in0(xor_2_out), .in1(adder_2_out), .out(Bit1), .sel(or_4_out));  // open: en
  not not_7 (not_7_out, or_4_out);
  or or_5 (or_5_out, Bit3, Bit2, Bit1);
  // _7_segment_display_driver 7_segment_display_driver_1: pin names not known; wires that end beside it: 1'b0, Bit3, Bit2, Bit1, n7_segment_display_driver_1_p5, n7_segment_display_driver_1_p6, n7_segment_display_driver_1_p7, n7_segment_display_driver_1_p8, n7_segment_display_driver_1_p9, n7_segment_display_driver_1_p10, n7_segment_display_driver_1_p11
  and and_8 (Sign, multiplexer_5_out, or_5_out);
  Multiplexer multiplexer_5 (.in0(multiplexer_1_out), .in1(S1), .out(multiplexer_5_out), .sel(or_4_out));  // open: en
  _7_Segment_Display u_7_segment_display_1 (
    .g(n7_segment_display_driver_1_p11), .f(n7_segment_display_driver_1_p10),
    .a(n7_segment_display_driver_1_p5), .b(n7_segment_display_driver_1_p6),
    .e(n7_segment_display_driver_1_p9), .d(n7_segment_display_driver_1_p8), .c(n7_segment_display_driver_1_p7));  // open: dp
  _7_Segment_Display u_7_segment_display_2 (.g(Sign));  // open: f, a, b, e, d, c, dp

  // Notes on the sheet:
  //   Bit 2
  //   Bit 1
endmodule
